# Fritzing sketch dooralarm (saved by Fritzing 0.9.1b)
breadboards: 1

parts:
  Raspberry_Pi3 = Raspberry Pi B+
  S2 = Pushbutton [package="[THT]"]
  R1 = Resistor [tolerance=±5% resistance=10k package="0805 [SMD]"]

nets:
  N1: Raspberry_Pi3.3v3, Raspberry_Pi3.GPIO4, S2.Pin_1, S2.Pin_2, R1.Pin_0
  N2: Raspberry_Pi3.GND, R1.Pin_1
